# Fritzing sketch lampada EVAz (saved by Fritzing 0.9.3b)
breadboards: 1

parts:
  LED1 = RGB LED (com. cathode, rgb) [package="5 mm [THT]"]
  Tempo = Rotary Potentiometer (Small) [maximum_resistance=100kΩ package=THT]
  Intensità = Rotary Potentiometer (Small) [maximum_resistance=100kΩ package=THT]
  S1 = Pushbutton [package="[THT]"]
  R3 = Resistor [tolerance=±5% resistance=220 package=THT]
  Componente1 = Arduino Uno (Rev3)

nets:
  N1: LED1.red_anode, Componente1.D3_PWM
  N2: LED1.common_cathode, Tempo.leg1, Intensità.leg1, S1.Pin_3, S1.Pin_4, Componente1.GND
  N3: LED1.green_anode, Componente1.D5_PWM
  N4: LED1.blue_anode, Componente1.D6_PWM
  N5: Tempo.wiper, Componente1.A0
  N6: Tempo.leg2, Intensità.leg2, R3.Pin_1, Componente1.5V
  N7: Intensità.wiper, Componente1.A1
  N8: S1.Pin_1, S1.Pin_2, R3.Pin_0, Componente1.D2
